// Logisim project Lista3.circ as structural Verilog: 10 circuits, main circuit 01) Mult2bits
module _01__Mult2bits (
  input  e1,
  input  e0,
  input  e1_2,
  input  e0_2,
  output out_5,
  output out_6,
  output out_7,
  output out_8
);

  wire and_2_out, and_3_out, and_4_out, and_5_out;

  and and_1 (out_5, and_2_out, and_3_out);
  and and_2 (and_2_out, e1, e1_2);
  and and_3 (and_3_out, and_4_out, and_5_out);
  xor xor_1 (out_6, and_2_out, and_3_out);
  and and_4 (and_4_out, e1, e0_2);
  and and_5 (and_5_out, e0, e1_2);
  xor xor_2 (out_7, and_4_out, and_5_out);
  and and_6 (out_8, e0, e0_2);
endmodule

module _02__BCD_error (
  input  a,
  input  b,
  input  c,
  input  d
);

  wire and_1_out, and_2_out, or_1_out;

  and and_1 (and_1_out, a, c);
  and and_2 (and_2_out, a, b);
  or or_1 (or_1_out, and_1_out, and_2_out);
  _7_Segment_Display u_7_segment_display_1 (
    .g(or_1_out), .f(or_1_out), .a(or_1_out), .e(or_1_out), .d(or_1_out));  // open: b, c, dp
endmodule

module _03__Iguais_Diferentes_2bit (
  input  e1,
  input  e0,
  input  e1_2,
  input  e0_2,
  output out_5
);

  wire xnor_1_out, xnor_2_out;

  xnor xnor_1 (xnor_1_out, e1, e1_2);
  and and_1 (out_5, xnor_1_out, xnor_2_out);
  xnor xnor_2 (xnor_2_out, e0, e0_2);
endmodule

module _04__Compare_4bit (
  input  [3:0] A,
  input  [3:0] B,
  output out_3,
  output out_4,
  output out_5
);

  wire and_1_out, and_2_out, and_3_out, and_4_out, and_5_out, and_7_out, or_1_out, or_2_out, or_3_out,
       T0_out, T1_out, T2_out, xnor_1_out, xnor_2_out, xnor_3_out, xnor_4_out;

  xnor xnor_1 (xnor_1_out, B[0], A[0]);
  xnor xnor_2 (xnor_2_out, B[1], A[1]);
  xnor xnor_3 (xnor_3_out, B[2], A[2]);
  xnor xnor_4 (xnor_4_out, B[3], A[3]);
  and T0 (T0_out, ~A[0], B[0]);  // AND_Gate
  or or_1 (or_1_out, ~A[1], B[1]);  // OR_Gate
  and and_1 (and_1_out, ~A[1], B[1]);  // AND_Gate
  and and_2 (and_2_out, T1_out, or_2_out);
  or or_2 (or_2_out, ~A[2], B[2]);  // OR_Gate
  and and_3 (and_3_out, ~A[2], B[2]);  // AND_Gate
  and and_4 (and_4_out, T0_out, or_1_out);
  or T1 (T1_out, and_4_out, and_1_out);
  or T2 (T2_out, and_2_out, and_3_out);
  or or_3 (or_3_out, ~A[3], B[3]);  // OR_Gate
  and and_5 (and_5_out, ~A[3], B[3]);  // AND_Gate
  and and_6 (out_3, xnor_1_out, xnor_2_out, xnor_3_out, xnor_4_out);
  and and_7 (and_7_out, T2_out, or_3_out);
  or T3 (out_4, and_7_out, and_5_out);
  nor nor_1 (out_5, out_3, out_4);

  // Notes on the sheet:
  //   primeiro carry é só A0'B0
  //   Usou-se:
  //   Tx= Tx-1(Ax' + Bx) + Ax'Bx
  //   para achar o carry atual
  //   Subtrator normal, se houver um carry ao final da subtração, A < B
endmodule

module _04__v_2_Compare_4bit (
  input  a3,
  input  a2,
  input  a1,
  input  a0,
  input  b3,
  input  b2,
  input  b1,
  input  b0,
  output out_9,
  output out_10,
  output out_11
);

  wire and_1_out, and_2_out, and_3_out, and_4_out, and_5_out, and_6_out, and_7_out, xnor_1_out, xnor_2_out,
       xnor_3_out, xnor_4_out;

  and and_1 (and_1_out, ~a3, b3);  // AND_Gate
  xnor xnor_1 (xnor_1_out, a3, b3);
  and and_2 (and_2_out, ~a2, b2);  // AND_Gate
  and and_3 (and_3_out, ~a1, b1);  // AND_Gate
  xnor xnor_2 (xnor_2_out, a1, b1);
  and and_4 (and_4_out, ~a0, b0);  // AND_Gate
  xnor xnor_3 (xnor_3_out, a0, b0);
  and and_5 (and_5_out, xnor_1_out, and_2_out);
  and and_6 (and_6_out, xnor_1_out, xnor_4_out, and_3_out);
  xnor xnor_4 (xnor_4_out, a2, b2);
  and and_7 (and_7_out, xnor_4_out, xnor_1_out, xnor_2_out, and_4_out);
  or or_1 (out_9, and_1_out, and_5_out, and_6_out, and_7_out);
  and and_8 (out_10, xnor_4_out, xnor_1_out, xnor_3_out, xnor_2_out);
  nor nor_1 (out_11, out_9, out_10);

  // Notes on the sheet:
  //   A < B se:
  //   A3 = 0  e B3 = 1 ou
  //   A3 = B3 e A2 = 0  e B2 = 1 ou
  //   A3 = B3 e A2 = B2 e A1 = 0 e B1 = 1 ou
  //   A3=B3 e A2=B2 e A1=B1 e A0=0 e B0=1
endmodule

module _05__Dec_BCD (
  input  p0,
  input  p1,
  input  p2,
  input  p3,
  input  p4,
  input  p5,
  input  p6,
  input  p7,
  input  p8,
  input  p9,
  output s3,
  output s2,
  output s1,
  output s0
);

  wire not_1_out, not_2_out, not_3_out, not_4_out, not_5_out, not_6_out, not_7_out, not_8_out, not_9_out,
       not_10_out, not_11_out, not_12_out, not_13_out, not_14_out, not_15_out, not_16_out, not_17_out,
       not_18_out, not_19_out, not_20_out, not_21_out, not_22_out, not_23_out, not_24_out, not_25_out;

  not not_1 (not_1_out, p0);
  not not_2 (not_2_out, p1);
  not not_3 (not_3_out, p2);
  not not_4 (not_4_out, p3);
  not not_5 (not_5_out, p4);
  not not_6 (not_6_out, p5);
  not not_7 (not_7_out, p6);
  not not_8 (not_8_out, p7);
  not not_9 (not_9_out, p0);
  not not_10 (not_10_out, p1);
  not not_11 (not_11_out, p2);
  not not_12 (not_12_out, p3);
  not not_13 (not_13_out, p8);
  not not_14 (not_14_out, p9);
  not not_15 (not_15_out, p0);
  not not_16 (not_16_out, p1);
  not not_17 (not_17_out, p4);
  not not_18 (not_18_out, p5);
  not not_19 (not_19_out, p8);
  not not_20 (not_20_out, p9);
  not not_21 (not_21_out, p0);
  not not_22 (not_22_out, p2);
  not not_23 (not_23_out, p4);
  not not_24 (not_24_out, p6);
  not not_25 (not_25_out, p8);
  and and_1 (s3, not_1_out, not_2_out, not_3_out, not_4_out, not_5_out, not_6_out, not_7_out, not_8_out);
  and and_2 (s2, not_9_out, not_10_out, not_11_out, not_12_out, not_13_out, not_14_out);
  and and_3 (s1, not_15_out, not_16_out, not_17_out, not_18_out, not_19_out, not_20_out);
  and and_4 (s0, not_21_out, not_22_out, not_23_out, not_24_out, not_25_out);
endmodule

module _8__4MUX_32MUX_e_4DEMUX_32DEMUX (
  input  [4:0] in_1,
  input  [4:0] in_2,
  input  [4:0] in_3,
  input  [4:0] in_4,
  input  [4:0] in_5,
  input  [4:0] in_6,
  input  [4:0] in_7,
  input  [4:0] in_8,
  input  [4:0] in_9,
  input  [4:0] in_10,
  input  [4:0] in_11,
  input  [4:0] in_12,
  input  [4:0] in_13,
  input  [4:0] in_14,
  input  [4:0] in_15,
  input  [4:0] in_16,
  input  [4:0] in_17,
  input  [4:0] in_18,
  input  [4:0] in_19,
  input  [4:0] in_20,
  input  [4:0] in_21,
  input  [4:0] in_22,
  input  [4:0] in_23,
  input  [4:0] in_24,
  input  [4:0] in_25,
  input  [4:0] in_26,
  input  [4:0] in_27,
  input  [4:0] in_28,
  input  [4:0] in_29,
  input  [4:0] in_30,
  input  [4:0] in_31,
  input  [4:0] in_32,
  input  [4:0] in_33,
  output [4:0] out_34,
  output [1:0] out_35,
  output [4:0] out_36,
  output [4:0] out_37,
  output [4:0] out_38,
  output [1:0] out_39,
  output [4:0] out_40,
  output [1:0] out_41,
  output [4:0] out_42,
  output [4:0] out_43,
  output [1:0] out_44,
  output [1:0] out_45,
  output [1:0] out_46,
  output [1:0] out_47,
  output [1:0] out_48,
  output [1:0] out_49,
  output [1:0] out_50
);

  wire [4:0] multiplexer_5_out, multiplexer_6_out, multiplexer_7_out, multiplexer_8_out;

  Multiplexer #(.select(2), .width(5), .enable("false")) multiplexer_1 (
    .in0(in_1), .in1(in_2), .in2(in_3), .in3(in_4), .out(out_34), .sel(in_5[1:0]));
  Multiplexer #(.select(2), .width(5), .enable("false")) multiplexer_2 (
    .in0(in_6), .in1(in_7), .in2(in_8), .in3(in_9), .out(out_36), .sel(in_5[1:0]));
  Multiplexer #(.select(2), .width(5), .enable("false")) multiplexer_3 (
    .in0(in_10), .in1(in_11), .in2(in_12), .in3(in_13), .out(out_38), .sel(in_5[1:0]));
  Multiplexer #(.select(2), .width(5), .enable("false")) multiplexer_4 (
    .in0(in_14), .in1(in_15), .in2(in_16), .in3(in_17), .out(out_42), .sel(in_5[1:0]));
  Multiplexer #(.select(2), .width(5), .enable("false")) multiplexer_5 (
    .in0(in_18), .in1(in_19), .in2(in_20), .in3(in_21), .out(multiplexer_5_out), .sel(in_5[1:0]));
  Multiplexer #(.select(2), .width(5), .enable("false")) multiplexer_6 (
    .in0(in_22), .in1(in_23), .in2(in_24), .in3(in_25), .out(multiplexer_6_out), .sel(in_5[1:0]));
  Multiplexer #(.select(2), .width(5), .enable("false")) multiplexer_7 (
    .in0(in_26), .in1(in_27), .in2(in_28), .in3(in_29), .out(multiplexer_7_out), .sel(in_5[1:0]));
  Multiplexer #(.select(2), .width(5), .enable("false")) multiplexer_8 (
    .in0(in_30), .in1(in_31), .in2(in_32), .in3(in_33), .out(multiplexer_8_out), .sel(in_5[1:0]));
  Multiplexer #(.select(2), .width(5), .enable("false")) multiplexer_9 (
    .in0(out_34), .in1(out_36), .in2(out_38), .in3(out_42), .out(out_37), .sel(in_5[3:2]));
  Multiplexer #(.select(2), .width(5), .enable("false")) multiplexer_10 (
    .in0(multiplexer_5_out), .in1(multiplexer_6_out), .in2(multiplexer_7_out), .in3(multiplexer_8_out),
    .out(out_43), .sel(in_5[3:2]));
  Multiplexer #(.select(2), .width(5), .enable("false")) multiplexer_11 (
    .in0(out_37), .in1(out_43), .out(out_40), .sel(out_44));  // open: in2, in3
  assign out_44 = {{1{1'b0}}, in_5[4]};  // Bit_Extender bit_extender_1

  assign out_35 = in_5[1:0];
  assign out_39 = in_5[3:2];
  assign out_41 = in_5[1:0];
  assign out_45 = in_5[1:0];
  assign out_46 = in_5[1:0];
  assign out_47 = in_5[1:0];
  assign out_48 = in_5[3:2];
  assign out_49 = in_5[1:0];
  assign out_50 = in_5[1:0];
endmodule

module _09__DEMUX_AND_e_OR (
  input  in_1,
  input  in_2,
  output AND,
  output OR
);

  Multiplexer #(.enable("false")) multiplexer_1 (.in0(1'b0), .in1(in_2), .out(AND), .sel(in_1));
  Multiplexer #(.enable("false")) multiplexer_2 (.in0(in_2), .in1(1'b1), .out(OR), .sel(in_1));
endmodule

module _10__MUX_Logic (
  input  A,
  input  b,
  input  c,
  output out_4
);

  Multiplexer #(.select(2), .enable("false")) multiplexer_1 (
    .in0(1'b0), .in1(A), .in2(A), .in3(1'b1), .out(out_4), .sel({b, c}));

  // Notes on the sheet:
  //   Se B=0 e C=0, a expressão anula
  //   Se B = 0 e C = 1, a expressão reduz para A
  //   O mesmo acontece com B=1 e C=0
  //   BC é verdadeiro
  //   EXP: A'BC + AB'C + ABC' + ABC.
  //   Simplificada: AB + AC + BC
endmodule

module _11__A_XOR_B_XOR_C__MUX (
  input  A,
  input  C,
  input  B,
  output S
);

  wire multiplexer_1_out, multiplexer_2_out, multiplexer_4_out;

  Multiplexer #(.enable("false")) multiplexer_1 (.in0(1'b1), .in1(1'b0), .out(multiplexer_1_out), .sel(A));
  Multiplexer #(.enable("false")) multiplexer_2 (.in0(A), .in1(multiplexer_1_out), .out(multiplexer_2_out), .sel(B));
  Multiplexer #(.enable("false")) multiplexer_3 (.in0(multiplexer_2_out), .in1(multiplexer_4_out), .out(S), .sel(C));
  Multiplexer #(.enable("false")) multiplexer_4 (
    .in0(1'b1), .in1(1'b0), .out(multiplexer_4_out), .sel(multiplexer_2_out));
endmodule
