// Logisim project Multiplicador 3 bits.circ as structural Verilog: 1 circuit, main circuit main
module main (
  input  A,
  input  B,
  input  C,
  input  D,
  input  E,
  input  F,
  output _32,
  output _16,
  output _8,
  output _4,
  output _2,
  output _1
);

  wire and_1_out, and_2_out, and_3_out, and_4_out, and_5_out, and_6_out, and_7_out, and_8_out, and_10_out,
       and_11_out, and_12_out, and_13_out, and_14_out, and_15_out, and_16_out, and_17_out, and_18_out,
       and_19_out, and_20_out, and_21_out, or_1_out, xor_2_out, xor_3_out, xor_4_out, xor_6_out, xor_7_out,
       xor_8_out;

  and and_1 (and_1_out, A, D);
  and and_2 (and_2_out, B, D);
  and and_3 (and_3_out, C, D);
  and and_4 (and_4_out, A, E);
  and and_5 (and_5_out, B, E);
  and and_6 (and_6_out, C, E);
  and and_7 (and_7_out, A, F);
  and and_8 (and_8_out, B, F);
  and and_9 (_1, C, F);
  and and_10 (and_10_out, and_6_out, and_8_out);
  xor xor_1 (_2, and_6_out, and_8_out);
  and and_11 (and_11_out, and_10_out, and_7_out);
  and and_12 (and_12_out, and_10_out, and_5_out);
  or or_1 (or_1_out, and_11_out, and_12_out, and_13_out);
  and and_13 (and_13_out, and_7_out, and_5_out);
  xor xor_2 (xor_2_out, and_5_out, and_7_out);
  xor xor_3 (xor_3_out, xor_2_out, and_10_out);
  and and_14 (and_14_out, or_1_out, and_15_out);
  xor xor_4 (xor_4_out, or_1_out, and_15_out);
  and and_15 (and_15_out, and_3_out, xor_3_out);
  xor xor_5 (_4, and_3_out, xor_3_out);
  and and_16 (and_16_out, and_20_out, and_14_out);
  and and_17 (and_17_out, and_20_out, and_19_out);
  and and_18 (and_18_out, and_14_out, and_19_out);
  xor xor_6 (xor_6_out, and_14_out, and_19_out);
  and and_19 (and_19_out, and_4_out, xor_4_out);
  xor xor_7 (xor_7_out, and_4_out, xor_4_out);
  xor xor_8 (xor_8_out, xor_6_out, and_20_out);
  and and_20 (and_20_out, and_2_out, xor_7_out);
  xor xor_9 (_8, and_2_out, xor_7_out);
  or or_2 (_32, and_16_out, and_17_out, and_18_out, and_21_out);
  and and_21 (and_21_out, and_1_out, xor_8_out);
  xor xor_10 (_16, and_1_out, xor_8_out);
endmodule
