// Logisim project Questao 3 lista 3.circ as structural Verilog: 1 circuit, main circuit main
module main (
  input  in_1,
  input  in_2,
  input  in_3,
  input  in_4,
  output out_5
);

  wire xnor_1_out, xnor_2_out;

  xnor xnor_1 (xnor_1_out, in_1, in_3);
  xnor xnor_2 (xnor_2_out, in_2, in_4);
  and and_1 (out_5, xnor_1_out, xnor_2_out);
endmodule
