// Logisim project Questao 4 lista 3.circ as structural Verilog: 1 circuit, main circuit main
module main (
  input  in_1,
  input  A,
  input  in_3,
  input  in_4,
  input  in_5,
  input  B,
  input  in_7,
  input  in_8,
  output A___B,
  output A___B_2,
  output A___B_3
);

  wire and_1_out, and_2_out, and_3_out, and_5_out, and_6_out, and_7_out, and_8_out, or_1_out, or_2_out,
       xnor_1_out, xnor_2_out, xnor_3_out, xnor_4_out, xor_1_out, xor_2_out, xor_3_out;

  xnor xnor_1 (xnor_1_out, in_1, in_5);
  xnor xnor_2 (xnor_2_out, A, B);
  xnor xnor_3 (xnor_3_out, in_3, in_7);
  xnor xnor_4 (xnor_4_out, in_4, in_8);
  and and_1 (and_1_out, ~in_4, in_8);  // AND_Gate
  and and_2 (and_2_out, B, or_1_out);
  and and_3 (and_3_out, in_7, and_1_out);
  and and_4 (A___B, xnor_1_out, xnor_2_out, xnor_3_out, xnor_4_out);
  xor xor_1 (xor_1_out, in_7, and_1_out);
  xor xor_2 (xor_2_out, B, or_1_out);
  and and_5 (and_5_out, ~in_3, xor_1_out);  // AND_Gate
  and and_6 (and_6_out, in_5, or_2_out);
  and and_7 (and_7_out, ~A, xor_2_out);  // AND_Gate
  or or_1 (or_1_out, and_3_out, and_5_out);
  or or_2 (or_2_out, and_2_out, and_7_out);
  xor xor_3 (xor_3_out, in_5, or_2_out);
  and and_8 (and_8_out, ~in_1, xor_3_out);  // AND_Gate
  or or_3 (A___B_2, and_6_out, and_8_out);
  nor nor_1 (A___B_3, A___B, A___B_2);
endmodule
