// Logisim project Questao 6 lista 3.circ as structural Verilog: 1 circuit, main circuit main
module main (
  input  in_1,
  input  in_2,
  input  in_3,
  input  in_4,
  input  in_5,
  input  in_6,
  input  in_7,
  input  in_8,
  output out_9
);

  wire multiplexer_1_out;

  Multiplexer #(.select(4), .enable("false")) multiplexer_1 (
    .in0(1'b0), .in1(1'b0), .in2(1'b0), .in3(1'b0), .in4(1'b0), .in5(1'b0), .in6(1'b0), .in7(1'b0),
    .in8(1'b0), .in9(1'b0), .in10(1'b1), .in11(1'b1), .in12(1'b1), .in13(1'b1), .in14(1'b1), .in15(1'b1),
    .out(multiplexer_1_out), .sel({in_1, in_2, in_3, in_4}));
  _7_Segment_Display u_7_segment_display_1 (
    .g(multiplexer_1_out), .f(multiplexer_1_out), .a(multiplexer_1_out), .e(multiplexer_1_out),
    .d(multiplexer_1_out));  // open: b, c, dp
  Multiplexer #(.select(4), .enable("false")) multiplexer_2 (
    .in0(1'b1), .in1(1'b0), .in2(1'b0), .in3(1'b0), .in4(1'b0), .in5(1'b1), .in6(1'b0), .in7(1'b0),
    .in8(1'b0), .in9(1'b0), .in10(1'b1), .in11(1'b0), .in12(1'b0), .in13(1'b0), .in14(1'b0), .in15(1'b1),
    .out(out_9), .sel({in_5, in_6, in_7, in_8}));

  // Notes on the sheet:
  //   MUX - 1
  //   MUX - 2
  //   MUX - 3 
endmodule
