// Logisim project Questao 8 lista 3.circ as structural Verilog: 1 circuit, main circuit main
module main (
  input  [4:0] in_1,
  input  [4:0] in_2,
  input  [4:0] in_3,
  input  [4:0] in_4,
  input  A,
  input  B,
  input  C,
  input  D,
  input  E,
  input  [4:0] in_10,
  input  [4:0] in_11,
  input  [4:0] in_12,
  input  [4:0] in_13,
  input  [4:0] in_14,
  input  [4:0] in_15,
  input  [4:0] in_16,
  input  [4:0] in_17,
  input  [4:0] in_18,
  input  [4:0] in_19,
  input  [4:0] in_20,
  input  [4:0] in_21,
  input  [4:0] in_22,
  input  [4:0] in_23,
  input  [4:0] in_24,
  input  [4:0] in_25,
  input  [4:0] in_26,
  input  [4:0] in_27,
  input  [4:0] in_28,
  input  [4:0] in_29,
  input  [4:0] in_30,
  input  [4:0] in_31,
  input  [4:0] in_32,
  input  [4:0] in_33,
  input  [4:0] in_34,
  input  [4:0] in_35,
  input  [4:0] in_36,
  input  [4:0] in_37,
  output [4:0] out_38
);

  wire [4:0] multiplexer_1_out, multiplexer_2_out, multiplexer_3_out, multiplexer_4_out, multiplexer_5_out,
       multiplexer_6_out, multiplexer_7_out, multiplexer_8_out, multiplexer_9_out, multiplexer_10_out;

  Multiplexer #(.select(2), .width(5), .enable("false")) multiplexer_1 (
    .in0(in_1), .in1(in_2), .in2(in_3), .in3(in_4), .out(multiplexer_1_out), .sel({D, E}));
  Multiplexer #(.select(2), .width(5), .enable("false")) multiplexer_2 (
    .in0(in_10), .in1(in_11), .in2(in_12), .in3(in_13), .out(multiplexer_2_out), .sel({D, E}));
  Multiplexer #(.select(2), .width(5), .enable("false")) multiplexer_3 (
    .in0(in_14), .in1(in_15), .in2(in_16), .in3(in_17), .out(multiplexer_3_out), .sel({D, E}));
  Multiplexer #(.select(2), .width(5), .enable("false")) multiplexer_4 (
    .in0(in_18), .in1(in_19), .in2(in_20), .in3(in_21), .out(multiplexer_4_out), .sel({D, E}));
  Multiplexer #(.select(2), .width(5), .enable("false")) multiplexer_5 (
    .in0(in_22), .in1(in_23), .in2(in_24), .in3(in_25), .out(multiplexer_5_out), .sel({D, E}));
  Multiplexer #(.select(2), .width(5), .enable("false")) multiplexer_6 (
    .in0(in_26), .in1(in_27), .in2(in_28), .in3(in_29), .out(multiplexer_6_out), .sel({D, E}));
  Multiplexer #(.select(2), .width(5), .enable("false")) multiplexer_7 (
    .in0(in_30), .in1(in_31), .in2(in_32), .in3(in_33), .out(multiplexer_7_out), .sel({D, E}));
  Multiplexer #(.select(2), .width(5), .enable("false")) multiplexer_8 (
    .in0(in_34), .in1(in_35), .in2(in_36), .in3(in_37), .out(multiplexer_8_out), .sel({D, E}));
  Multiplexer #(.select(2), .width(5), .enable("false")) multiplexer_9 (
    .in0(multiplexer_1_out), .in1(multiplexer_2_out), .in2(multiplexer_3_out), .in3(multiplexer_4_out),
    .out(multiplexer_9_out), .sel({B, C}));
  Multiplexer #(.select(2), .width(5), .enable("false")) multiplexer_10 (
    .in0(multiplexer_5_out), .in1(multiplexer_6_out), .in2(multiplexer_7_out), .in3(multiplexer_8_out),
    .out(multiplexer_10_out), .sel({B, C}));
  Multiplexer #(.select(2), .width(5), .enable("false")) multiplexer_11 (
    .in0(multiplexer_9_out), .in3(multiplexer_10_out), .out(out_38), .sel({2{A}}));  // open: in1, in2
endmodule
