// Logisim project Questao 9 lista 3.circ as structural Verilog: 1 circuit, main circuit main
module main (
  input  S___A____B,
  input  B,
  input  in_3,
  input  A,
  output out_5,
  output out_6
);

  Multiplexer #(.enable("false")) multiplexer_1 (.in0(1'b0), .in1(B), .out(out_6), .sel(A));
  Multiplexer #(.enable("false")) multiplexer_2 (.in0(S___A____B), .in1(1'b1), .out(out_5), .sel(in_3));

  // Notes on the sheet:
  //   S = AB
endmodule
