// Logisim project Questão 1.circ as structural Verilog: 1 circuit, main circuit main
module main (
  input  A,
  input  B,
  input  C,
  input  D,
  output out_5,
  output out_6,
  output out_7,
  output out_8
);

  wire and_1_out, and_2_out, and_3_out, and_5_out;

  and and_1 (and_1_out, C, A);
  and and_2 (and_2_out, D, A);
  and and_3 (and_3_out, C, B);
  and and_4 (out_8, D, B);
  and and_5 (and_5_out, and_3_out, and_2_out);
  and and_6 (out_5, and_5_out, and_1_out);
  xor xor_1 (out_6, and_1_out, and_5_out);
  xor xor_2 (out_7, and_2_out, and_3_out);
endmodule
