// Logisim project Questão 2.circ as structural Verilog: 1 circuit, main circuit main
module main (
  input  A,
  input  B,
  input  C,
  input  D
);

  wire and_1_out, and_2_out, and_3_out, and_4_out, and_5_out, and_6_out, not_1_out, not_2_out, not_3_out,
       not_4_out, not_5_out, not_6_out, not_7_out, or_1_out, or_2_out, or_3_out;

  not not_1 (not_1_out, B);
  not not_2 (not_2_out, D);
  not not_3 (not_3_out, B);
  not not_4 (not_4_out, C);
  not not_5 (not_5_out, D);
  not not_6 (not_6_out, C);
  not not_7 (not_7_out, D);
  and and_1 (and_1_out, A, not_1_out, C, not_2_out);
  and and_2 (and_2_out, A, not_3_out, C, D);
  and and_3 (and_3_out, A, B, not_4_out, not_5_out);
  and and_4 (and_4_out, A, B, not_6_out, D);
  and and_5 (and_5_out, A, B, C, not_7_out);
  and and_6 (and_6_out, A, B, C, D);
  or or_1 (or_1_out, and_1_out, and_2_out, and_3_out);
  or or_2 (or_2_out, and_4_out, and_5_out, and_6_out);
  or or_3 (or_3_out, or_1_out, or_2_out);
  _7_Segment_Display u_7_segment_display_1 (
    .g(or_3_out), .f(or_3_out), .a(or_3_out), .e(or_3_out), .d(or_3_out));  // open: b, c, dp
endmodule
