// Logisim project Questão 9.circ as structural Verilog: 1 circuit, main circuit main
module main (
  input  in_1,
  input  in_2,
  input  in_3,
  input  in_4,
  output out_5,
  output out_6
);

  wire multiplexer_2_out;

  Multiplexer multiplexer_1 (.in0(in_1), .in1(in_2), .out(out_5), .sel(in_1));  // open: en
  Multiplexer multiplexer_2 (.in0(in_3), .in1(in_4), .out(multiplexer_2_out), .sel(in_4));  // open: en
  Multiplexer multiplexer_3 (.in0(in_4), .in1(multiplexer_2_out), .out(out_6), .sel(multiplexer_2_out));  // open: en

  // Notes on the sheet:
  //   Falta esse, o somador com mux
endmodule
