// Logisim project Questão 2.circ as structural Verilog: 1 circuit, main circuit main
module main (
  input  in_1,
  input  in_2,
  input  in_3,
  input  in_4,
  input  in_5,
  input  in_6,
  input  in_7,
  input  in_8,
  input  in_9,
  input  in_10,
  input  in_11,
  input  in_12,
  input  in_13,
  input  in_14,
  input  in_15,
  input  in_16,
  input  in_17,
  input  in_18,
  input  in_19,
  input  in_20,
  output out_21
);

  wire and_1_out, and_2_out, and_3_out, and_4_out, and_5_out, and_6_out, and_7_out, and_8_out, and_9_out,
       and_10_out, and_11_out, and_12_out, and_13_out, and_14_out, and_15_out, and_16_out, not_1_out,
       not_2_out, not_3_out, not_4_out, or_1_out, or_2_out, or_3_out;

  not not_1 (not_1_out, in_17);
  not not_2 (not_2_out, in_18);
  not not_3 (not_3_out, in_19);
  not not_4 (not_4_out, in_20);
  and and_1 (and_1_out, not_1_out, not_2_out, not_3_out, not_4_out, in_1);
  and and_2 (and_2_out, not_1_out, not_2_out, in_19, not_4_out, in_3);
  and and_3 (and_3_out, not_1_out, in_18, not_3_out, not_4_out, in_5);
  and and_4 (and_4_out, not_1_out, in_18, in_19, not_4_out, in_7);
  and and_5 (and_5_out, in_17, not_2_out, not_3_out, not_4_out, in_9);
  and and_6 (and_6_out, in_17, not_2_out, in_19, not_4_out, in_11);
  and and_7 (and_7_out, in_17, in_18, not_3_out, not_4_out, in_13);
  and and_8 (and_8_out, in_17, in_18, in_19, not_4_out, in_15);
  and and_9 (and_9_out, not_1_out, not_2_out, not_3_out, in_20, in_2);
  and and_10 (and_10_out, not_1_out, not_2_out, in_19, in_20, in_4);
  and and_11 (and_11_out, not_1_out, in_18, not_3_out, in_20, in_6);
  and and_12 (and_12_out, not_1_out, in_18, in_19, in_20, in_8);
  and and_13 (and_13_out, in_17, not_2_out, not_3_out, in_20, in_10);
  and and_14 (and_14_out, in_17, not_2_out, in_19, in_20, in_12);
  and and_15 (and_15_out, in_17, in_18, not_3_out, in_20, in_14);
  and and_16 (and_16_out, in_17, in_18, in_19, in_20, in_16);
  or or_1 (or_1_out, and_1_out, and_9_out, and_2_out, and_10_out, and_3_out);
  or or_2 (or_2_out, and_11_out, and_4_out, and_12_out, and_5_out, and_13_out);
  or or_3 (or_3_out, and_6_out, and_14_out, and_7_out, and_15_out, and_8_out);
  or or_4 (out_21, or_1_out, or_2_out, and_16_out, or_3_out);
endmodule
