// Logisim project Questão 3.circ as structural Verilog: 1 circuit, main circuit main
module main (
  input  B,
  input  A,
  input  C,
  input  D,
  output out_5
);

  wire multiplexer_1_out, multiplexer_2_out, not_1_out, not_2_out, not_3_out;

  not not_1 (not_1_out, B);
  Multiplexer multiplexer_1 (.in0(B), .in1(not_1_out), .out(multiplexer_1_out), .sel(A));  // open: en
  Multiplexer multiplexer_2 (.in0(multiplexer_1_out), .in1(not_2_out), .out(multiplexer_2_out), .sel(C));  // open: en
  not not_2 (not_2_out, multiplexer_1_out);
  not not_3 (not_3_out, multiplexer_2_out);
  Multiplexer multiplexer_3 (.in0(multiplexer_2_out), .in1(not_3_out), .out(out_5), .sel(D));  // open: en
endmodule
