// Logisim project Questão 4.circ as structural Verilog: 1 circuit, main circuit main
module main (
  input  A,
  input  B,
  input  C,
  input  D,
  input  E,
  input  F,
  output out_7,
  output out_8,
  output out_9,
  output out_10,
  output out_11,
  output out_12
);

  wire and_1_out, and_2_out, and_3_out, and_4_out, and_5_out, and_6_out, and_8_out, and_9_out, and_10_out,
       and_11_out, and_12_out, and_13_out, and_15_out, and_17_out, and_18_out, or_1_out, or_2_out, xor_1_out,
       xor_2_out, xor_3_out, xor_4_out, xor_6_out;

  and and_1 (and_1_out, E, A);
  and and_2 (and_2_out, D, B);
  and and_3 (and_3_out, F, A);
  and and_4 (and_4_out, B, E);
  and and_5 (and_5_out, C, E);
  and and_6 (and_6_out, F, B);
  and and_7 (out_12, C, F);
  xor xor_1 (xor_1_out, and_1_out, and_2_out);
  xor xor_2 (xor_2_out, xor_1_out, or_2_out);
  and and_8 (and_8_out, and_1_out, and_2_out);
  and and_9 (and_9_out, and_2_out, or_2_out);
  xor xor_3 (xor_3_out, and_3_out, and_4_out);
  and and_10 (and_10_out, and_3_out, and_4_out);
  and and_11 (and_11_out, and_3_out, and_13_out);
  and and_12 (and_12_out, and_4_out, and_13_out);
  and and_13 (and_13_out, and_5_out, and_6_out);
  and and_14 (out_8, D, A);
  or or_1 (or_1_out, and_8_out, and_9_out, and_15_out);
  and and_15 (and_15_out, and_1_out, or_2_out);
  xor xor_4 (xor_4_out, xor_3_out, and_13_out);
  or or_2 (or_2_out, and_10_out, and_11_out, and_12_out);
  xor xor_5 (out_11, and_5_out, and_6_out);
  // AND_Gate and_16 has open pins: in2=out_8, out=open
  and and_17 (and_17_out, D, C);
  xor xor_6 (xor_6_out, xor_2_out, and_18_out);
  xor xor_7 (out_10, xor_4_out, and_17_out);
  and and_18 (and_18_out, xor_4_out, and_17_out);
  buf xor_8 (out_9, xor_6_out);  // XOR_Gate
endmodule
