// Logisim project Projeto_PCL_Fase1_ULA.circ as structural Verilog: 3 circuits, main circuit ula
module ula (
  input  [7:0] Operando_1,
  input  [7:0] Operando_2,
  input  [3:0] Seletor,
  output [7:0] \Saída 
);

  wire comparator_1_eq, comparator_2_eq, comparator_3_lt, comparator_4_eq, comparator_4_lt, or_2_out;
  wire [7:0] adder_1_out, and_1_out, bit_extender_1_out, bit_extender_2_out, bit_extender_3_out,
       bit_extender_4_out, divider_1_out, multiplier_1_out, or_1_out, subtractor_1_out;

  assign and_1_out = Operando_1 & Operando_2;  // AND_Gate and_1, 8 bits wide
  assign or_1_out = Operando_1 | Operando_2;  // OR_Gate or_1, 8 bits wide
  Comparator comparator_1 (.a(Operando_1), .b({8{1'b0}}), .eq(comparator_1_eq));  // open: gt, lt
  Adder adder_1 (.a(Operando_1), .b(Operando_2), .out(adder_1_out));  // open: cin, cout
  Subtractor subtractor_1 (.a(Operando_1), .b(Operando_2), .out(subtractor_1_out));  // open: bin, bout
  Multiplier multiplier_1 (.a(Operando_1), .b(Operando_2), .out(multiplier_1_out));  // open: cin, cout
  Divider divider_1 (.a(Operando_1), .b(Operando_2), .out(divider_1_out));  // open: upper, rem
  Comparator comparator_2 (.a(Operando_1), .b(Operando_2), .eq(comparator_2_eq));  // open: gt, lt
  Comparator comparator_3 (.a(Operando_1), .b(Operando_2), .lt(comparator_3_lt));  // open: gt, eq
  Comparator comparator_4 (.a(Operando_1), .b(Operando_2), .eq(comparator_4_eq), .lt(comparator_4_lt));  // open: gt
  assign bit_extender_1_out = {{7{1'b0}}, comparator_1_eq};  // Bit_Extender bit_extender_1
  assign bit_extender_2_out = {{7{1'b0}}, comparator_2_eq};  // Bit_Extender bit_extender_2
  assign bit_extender_3_out = {{7{1'b0}}, comparator_3_lt};  // Bit_Extender bit_extender_3
  or or_2 (or_2_out, comparator_4_eq, comparator_4_lt);
  assign bit_extender_4_out = {{7{1'b0}}, or_2_out};  // Bit_Extender bit_extender_4
  Multiplexer #(.select(4), .width(8), .enable("false")) multiplexer_1 (
    .in0(and_1_out), .in1(or_1_out), .in2(bit_extender_1_out), .in3(adder_1_out), .in4(subtractor_1_out),
    .in5(multiplier_1_out), .in6(divider_1_out), .in7(bit_extender_2_out), .in8(bit_extender_3_out),
    .in9(bit_extender_4_out), .out(\Saída ), .sel(Seletor));  // open: in10, in11, in12, in13, in14, in15

  // Notes on the sheet:
  //   E 0000
  //   Ou 0001
  //   Não Logico 0010
  //   Add 0011
  //   sub 0100
  //   Mult. 0101
  //   Div.  0110
  //   Igual 0111
  //   Menor 1000
  //   Menor igual 1001
  //   João Lucas Lima de Melo PCL 2019.1
endmodule

module Registrador (
  input  [7:0] Entrada_de_Dados,
  input  write,
  input  [3:0] Seletor_A,
  input  [3:0] Seletor_w,
  input  [3:0] Seletor_B,
  output [7:0] \Saída_A ,
  output [7:0] \Saída_B 
);

  wire clock_1_out, demultiplexer_1_out0, demultiplexer_1_out1, demultiplexer_1_out2, demultiplexer_1_out3,
       demultiplexer_1_out4, demultiplexer_1_out5, demultiplexer_1_out6, demultiplexer_1_out7,
       demultiplexer_1_out8, demultiplexer_1_out9, demultiplexer_1_out10, demultiplexer_1_out11,
       demultiplexer_1_out12, demultiplexer_1_out13, demultiplexer_1_out14, demultiplexer_1_out15;
  wire [7:0] R0_q, register_1_q, register_2_q, register_3_q, register_4_q, register_5_q, register_6_q,
       register_7_q, register_8_q, register_9_q, register_10_q, register_11_q, register_12_q, register_13_q,
       register_14_q, register_15_q;

  Demultiplexer #(.select(4), .enable("false")) demultiplexer_1 (
    .out0(demultiplexer_1_out0), .out1(demultiplexer_1_out1), .out2(demultiplexer_1_out2),
    .out3(demultiplexer_1_out3), .out4(demultiplexer_1_out4), .out5(demultiplexer_1_out5),
    .out6(demultiplexer_1_out6), .out7(demultiplexer_1_out7), .out8(demultiplexer_1_out8),
    .out9(demultiplexer_1_out9), .out10(demultiplexer_1_out10), .out11(demultiplexer_1_out11),
    .out12(demultiplexer_1_out12), .out13(demultiplexer_1_out13), .out14(demultiplexer_1_out14),
    .out15(demultiplexer_1_out15), .in(write), .sel(Seletor_w));
  Clock clock_1 (.out(clock_1_out));
  Register R0 (.D(Entrada_de_Dados), .en(demultiplexer_1_out0), .Q(R0_q), .clk(clock_1_out));  // open: clr
  Register register_1 (
    .D(Entrada_de_Dados), .en(demultiplexer_1_out1), .Q(register_1_q), .clk(clock_1_out));  // open: clr
  Register register_2 (
    .D(Entrada_de_Dados), .en(demultiplexer_1_out2), .Q(register_2_q), .clk(clock_1_out));  // open: clr
  Register register_3 (
    .D(Entrada_de_Dados), .en(demultiplexer_1_out3), .Q(register_3_q), .clk(clock_1_out));  // open: clr
  Register register_4 (
    .D(Entrada_de_Dados), .en(demultiplexer_1_out4), .Q(register_4_q), .clk(clock_1_out));  // open: clr
  Register register_5 (
    .D(Entrada_de_Dados), .en(demultiplexer_1_out5), .Q(register_5_q), .clk(clock_1_out));  // open: clr
  Register register_6 (
    .D(Entrada_de_Dados), .en(demultiplexer_1_out6), .Q(register_6_q), .clk(clock_1_out));  // open: clr
  Register register_7 (
    .D(Entrada_de_Dados), .en(demultiplexer_1_out7), .Q(register_7_q), .clk(clock_1_out));  // open: clr
  Register register_8 (
    .D(Entrada_de_Dados), .en(demultiplexer_1_out8), .Q(register_8_q), .clk(clock_1_out));  // open: clr
  Register register_9 (
    .D(Entrada_de_Dados), .en(demultiplexer_1_out9), .Q(register_9_q), .clk(clock_1_out));  // open: clr
  Register register_10 (
    .D(Entrada_de_Dados), .en(demultiplexer_1_out10), .Q(register_10_q), .clk(clock_1_out));  // open: clr
  Register register_11 (
    .D(Entrada_de_Dados), .en(demultiplexer_1_out11), .Q(register_11_q), .clk(clock_1_out));  // open: clr
  Register register_12 (
    .D(Entrada_de_Dados), .en(demultiplexer_1_out12), .Q(register_12_q), .clk(clock_1_out));  // open: clr
  Register register_13 (
    .D(Entrada_de_Dados), .en(demultiplexer_1_out13), .Q(register_13_q), .clk(clock_1_out));  // open: clr
  Register register_14 (
    .D(Entrada_de_Dados), .en(demultiplexer_1_out14), .Q(register_14_q), .clk(clock_1_out));  // open: clr
  Register register_15 (
    .D(Entrada_de_Dados), .en(demultiplexer_1_out15), .Q(register_15_q), .clk(clock_1_out));  // open: clr
  Multiplexer #(.select(4), .width(8), .enable("false")) multiplexer_1 (
    .in0(R0_q), .in1(register_1_q), .in2(register_2_q), .in3(register_3_q), .in4(register_4_q),
    .in5(register_5_q), .in6(register_6_q), .in7(register_7_q), .in8(register_8_q), .in9(register_9_q),
    .in10(register_10_q), .in11(register_11_q), .in12(register_12_q), .in13(register_13_q),
    .in14(register_14_q), .in15(register_15_q), .out(\Saída_A ), .sel(Seletor_A));
  Multiplexer #(.select(4), .width(8), .enable("false")) multiplexer_2 (
    .in0(R0_q), .in1(register_1_q), .in2(register_2_q), .in3(register_3_q), .in4(register_4_q),
    .in5(register_5_q), .in6(register_6_q), .in7(register_7_q), .in8(register_8_q), .in9(register_9_q),
    .in10(register_10_q), .in11(register_11_q), .in12(register_12_q), .in13(register_13_q),
    .in14(register_14_q), .in15(register_15_q), .out(\Saída_B ), .sel(Seletor_B));
endmodule

module teste (
  input  Write,
  input  [3:0] Seletor_w,
  input  [3:0] Seletor_ULA,
  input  [3:0] Seletor_A,
  input  [3:0] Seletor_B
);

  wire [7:0] \registrador_1_saída_a , \registrador_1_saída_b , \ula_1_saída ;

  Registrador registrador_1 (
    .write(Write), .Seletor_w(Seletor_w), .Seletor_A(Seletor_A), .Seletor_B(Seletor_B),
    .\Saída_A (\registrador_1_saída_a ), .\Saída_B (\registrador_1_saída_b ));  // open: Entrada_de_Dados
  ula ula_1 (
    .Operando_1(\registrador_1_saída_a ), .Operando_2(\registrador_1_saída_b ), .Seletor(Seletor_ULA),
    .\Saída (\ula_1_saída ));
endmodule
