// Logisim project Lista4.circ as structural Verilog: 10 circuits, main circuit 03) 16-KHZ -> 2KHZ
module _03__16_KHZ____2KHZ (
  output out_1
);

  wire clock_1_out, t_ff_1_q, t_ff_1_qn, t_ff_3_q, t_ff_3_qn, t_ff_4_q;

  Clock clock_1 (.out(clock_1_out));
  T_Flip_Flop t_ff_1 (.clk(clock_1_out), .T(1'b1), .Q(t_ff_1_q), .Qn(t_ff_1_qn));  // open: preset, reset, en
  T_Flip_Flop t_ff_2 ();  // open: clk, T, Q, Qn, preset, reset, en
  and and_1 (out_1, t_ff_1_q, t_ff_3_q, t_ff_4_q);
  T_Flip_Flop t_ff_3 (.clk(t_ff_1_qn), .T(1'b1), .Q(t_ff_3_q), .Qn(t_ff_3_qn));  // open: preset, reset, en
  T_Flip_Flop t_ff_4 (.clk(t_ff_3_qn), .T(1'b1), .Q(t_ff_4_q));  // open: Qn, preset, reset, en

  // Notes on the sheet:
  //   A cada 8 pulsadas, CLK1 recebe 1 pulsada, logo 16KHZ/8 = 2KHZ
endmodule

module _04__Contador_0_10 (
);

  wire and_1_out, clock_1_out, t_ff_1_q, t_ff_1_qn, t_ff_2_q, t_ff_2_qn, t_ff_3_q, t_ff_3_qn, t_ff_4_q;

  Clock clock_1 (.out(clock_1_out));
  T_Flip_Flop t_ff_1 (
    .clk(clock_1_out), .T(1'b1), .Q(t_ff_1_q), .Qn(t_ff_1_qn), .reset(and_1_out));  // open: preset, en
  T_Flip_Flop t_ff_2 (.clk(t_ff_1_qn), .T(1'b1), .Q(t_ff_2_q), .Qn(t_ff_2_qn), .reset(and_1_out));  // open: preset, en
  T_Flip_Flop t_ff_3 (.clk(t_ff_2_qn), .T(1'b1), .Q(t_ff_3_q), .Qn(t_ff_3_qn), .reset(and_1_out));  // open: preset, en
  and and_1 (and_1_out, t_ff_1_q, t_ff_2_q, ~t_ff_3_q, t_ff_4_q);  // AND_Gate
  T_Flip_Flop t_ff_4 (.clk(t_ff_3_qn), .T(1'b1), .Q(t_ff_4_q), .reset(and_1_out));  // open: Qn, preset, en
endmodule

module _05__Contador_0_10_e_10_0 (
  input  Desc,
  output [3:0] out_2
);

  wire and_1_out, clock_1_out, t_ff_1_q, t_ff_1_qn, t_ff_2_q, t_ff_2_qn, t_ff_3_q, t_ff_3_qn, t_ff_4_q;
  wire [3:0] subtractor_1_out, xor_1_out;

  Clock clock_1 (.out(clock_1_out));
  T_Flip_Flop t_ff_1 (
    .clk(clock_1_out), .T(1'b1), .Q(t_ff_1_q), .Qn(t_ff_1_qn), .reset(and_1_out));  // open: preset, en
  xor xor_1 (xor_1_out[0], Desc, t_ff_1_q);
  T_Flip_Flop t_ff_2 (.clk(t_ff_1_qn), .T(1'b1), .Q(t_ff_2_q), .Qn(t_ff_2_qn), .reset(and_1_out));  // open: preset, en
  xor xor_2 (xor_1_out[1], Desc, t_ff_2_q);
  T_Flip_Flop t_ff_3 (.clk(t_ff_2_qn), .T(1'b1), .Q(t_ff_3_q), .Qn(t_ff_3_qn), .reset(and_1_out));  // open: preset, en
  and and_1 (and_1_out, t_ff_1_q, t_ff_2_q, ~t_ff_3_q, t_ff_4_q);  // AND_Gate
  xor xor_3 (xor_1_out[2], Desc, t_ff_3_q);
  T_Flip_Flop t_ff_4 (.clk(t_ff_3_qn), .T(1'b1), .Q(t_ff_4_q), .reset(and_1_out));  // open: Qn, preset, en
  xor xor_4 (xor_1_out[3], Desc, t_ff_4_q);
  Subtractor #(.width(4)) subtractor_1 (.a(xor_1_out), .b(4'b0101), .out(subtractor_1_out));  // open: bin, bout
  Multiplexer #(.width(4), .enable("false")) multiplexer_1 (
    .in0(xor_1_out), .in1(subtractor_1_out), .out(out_2), .sel(Desc));
endmodule

module _07__Contador_1____2____7____8____12____15____1 (
);

  wire clock_1_out, j_k_ff_1_q, j_k_ff_1_qn, j_k_ff_2_q, j_k_ff_3_q, j_k_ff_4_qn, or_1_out;

  Clock clock_1 (.out(clock_1_out));
  J_K_Flip_Flop j_k_ff_1 (
    .J(or_1_out), .clk(clock_1_out), .K(j_k_ff_4_qn), .Q(j_k_ff_1_q), .Qn(j_k_ff_1_qn));  // open: preset, en, reset
  or or_1 (or_1_out, j_k_ff_4_qn, j_k_ff_3_q);
  J_K_Flip_Flop j_k_ff_2 (
    .J(or_1_out), .clk(clock_1_out), .K(j_k_ff_1_q), .Q(j_k_ff_2_q));  // open: Qn, preset, en, reset
  J_K_Flip_Flop j_k_ff_3 (
    .J(j_k_ff_1_qn), .clk(clock_1_out), .K(j_k_ff_2_q), .Q(j_k_ff_3_q));  // open: Qn, preset, en, reset
  J_K_Flip_Flop j_k_ff_4 (
    .J(j_k_ff_3_q), .clk(clock_1_out), .K(j_k_ff_2_q), .Qn(j_k_ff_4_qn));  // open: Q, preset, en, reset
endmodule

module _07___Tabela_Verdade (
  input  q3,
  input  q2,
  input  q1,
  input  q0,
  output j3,
  output k3,
  output j2,
  output k2,
  output j1,
  output k1,
  output j0,
  output k0
);

  wire not_2_out, not_3_out;

  not not_1 (j2, q0);
  not not_2 (not_2_out, q3);
  or or_1 (j1, not_2_out, q2);
  not not_3 (not_3_out, q3);
  or or_2 (j0, not_3_out, q2);
  not not_4 (k0, q3);

  assign j3 = q2;
  assign k1 = q2;
  assign k2 = q1;
  assign k3 = q1;
endmodule

module _08__0_7__7_0__sincrono (
  input  Desc,
  output Q2,
  output Q1,
  output Q0
);

  wire and_1_out, clock_1_out, j_k_ff_1_q, j_k_ff_2_q, j_k_ff_3_q;

  Clock clock_1 (.out(clock_1_out));
  xor xor_1 (Q2, Desc, j_k_ff_1_q);
  J_K_Flip_Flop j_k_ff_1 (.J(1'b1), .clk(clock_1_out), .K(1'b1), .Q(j_k_ff_1_q));  // open: Qn, preset, en, reset
  xor xor_2 (Q1, Desc, j_k_ff_2_q);
  J_K_Flip_Flop j_k_ff_2 (
    .J(j_k_ff_1_q), .clk(clock_1_out), .K(j_k_ff_1_q), .Q(j_k_ff_2_q));  // open: Qn, preset, en, reset
  xor xor_3 (Q0, Desc, j_k_ff_3_q);
  and and_1 (and_1_out, j_k_ff_2_q, j_k_ff_1_q);
  J_K_Flip_Flop j_k_ff_3 (
    .J(and_1_out), .clk(clock_1_out), .K(and_1_out), .Q(j_k_ff_3_q));  // open: Qn, preset, en, reset
endmodule

module _08___Tabela_Verdade (
  input  q2,
  input  q1,
  input  q0,
  output j2,
  output k2,
  output j1,
  output k1,
  output j0,
  output k0
);

  and and_1 (j2, q1, q0);
  and and_2 (k2, q1, q0);

  assign j0 = 1'b1;
  assign j1 = q0;
  assign k0 = 1'b1;
  assign k1 = q0;
endmodule

module _09__Contador_0___1___3___7___15___14___12___8___0 (
);

  wire and_1_out, clock_1_out, j_k_ff_1_q, j_k_ff_1_qn, j_k_ff_2_q, j_k_ff_2_qn, j_k_ff_3_q, j_k_ff_3_qn,
       j_k_ff_4_q, j_k_ff_4_qn, or_1_out;

  Clock clock_1 (.out(clock_1_out));
  and and_1 (and_1_out, j_k_ff_1_q, j_k_ff_2_qn);
  J_K_Flip_Flop j_k_ff_1 (
    .J(j_k_ff_4_qn), .clk(clock_1_out), .K(j_k_ff_4_q), .Q(j_k_ff_1_q), .Qn(j_k_ff_1_qn));  // open: preset, en, reset
  J_K_Flip_Flop j_k_ff_2 (
    .J(and_1_out), .clk(clock_1_out), .K(j_k_ff_1_qn), .Q(j_k_ff_2_q), .Qn(j_k_ff_2_qn));  // open: preset, en, reset
  J_K_Flip_Flop j_k_ff_3 (
    .J(j_k_ff_2_q), .clk(clock_1_out), .K(j_k_ff_2_qn), .Q(j_k_ff_3_q), .Qn(j_k_ff_3_qn));  // open: preset, en, reset
  or or_1 (or_1_out, j_k_ff_3_q, j_k_ff_4_q);
  J_K_Flip_Flop j_k_ff_4 (
    .J(or_1_out), .clk(clock_1_out), .K(j_k_ff_3_qn), .Q(j_k_ff_4_q), .Qn(j_k_ff_4_qn));  // open: preset, en, reset
endmodule

module _09___Tabela_Verdade (
  input  q3,
  input  q2,
  input  q1,
  input  q0,
  output j3,
  output k3,
  output j2,
  output k2,
  output j1,
  output k1,
  output j0,
  output k0
);

  wire not_3_out;

  not not_1 (k3, q2);
  not not_2 (k2, q1);
  not not_3 (not_3_out, q1);
  and and_1 (j1, not_3_out, q0);
  not not_4 (k1, q0);
  not not_5 (j0, q3);

  assign j2 = q1;
  assign j3 = q2;
  assign k0 = q3;
endmodule

module _10__Deslocamento_D_FlipFlop (
  input  Q3,
  input  Q2,
  input  Q1,
  input  Q0,
  input  ModoCarga,
  output \Saída 
);

  wire clock_1_out, controlled_buffer_1_out, controlled_buffer_2_out, controlled_buffer_3_out,
       controlled_buffer_4_out, controlled_inverter_1_out, controlled_inverter_2_out,
       controlled_inverter_3_out, controlled_inverter_4_out, d_ff_1_q, d_ff_2_q, d_ff_3_q;

  Clock clock_1 (.out(clock_1_out));
  assign controlled_buffer_1_out = ModoCarga ? Q3 : 1'bz;  // Controlled_Buffer controlled_buffer_1
  D_Flip_Flop d_ff_1 (
    .clk(clock_1_out), .D(\Saída ), .Q(d_ff_1_q), .preset(controlled_buffer_1_out),
    .reset(controlled_inverter_1_out));  // open: Qn, en
  assign controlled_inverter_1_out = ModoCarga ? ~Q3 : 1'bz;  // Controlled_Inverter controlled_inverter_1
  D_Flip_Flop d_ff_2 (
    .clk(clock_1_out), .D(d_ff_1_q), .Q(d_ff_2_q), .preset(controlled_buffer_2_out),
    .reset(controlled_inverter_2_out));  // open: Qn, en
  assign controlled_buffer_2_out = ModoCarga ? Q2 : 1'bz;  // Controlled_Buffer controlled_buffer_2
  assign controlled_inverter_2_out = ModoCarga ? ~Q2 : 1'bz;  // Controlled_Inverter controlled_inverter_2
  assign controlled_buffer_3_out = ModoCarga ? Q1 : 1'bz;  // Controlled_Buffer controlled_buffer_3
  D_Flip_Flop d_ff_3 (
    .clk(clock_1_out), .D(d_ff_2_q), .Q(d_ff_3_q), .preset(controlled_buffer_3_out),
    .reset(controlled_inverter_3_out));  // open: Qn, en
  assign controlled_inverter_3_out = ModoCarga ? ~Q1 : 1'bz;  // Controlled_Inverter controlled_inverter_3
  D_Flip_Flop d_ff_4 (
    .clk(clock_1_out), .D(d_ff_3_q), .Q(\Saída ), .preset(controlled_buffer_4_out),
    .reset(controlled_inverter_4_out));  // open: Qn, en
  assign controlled_inverter_4_out = ModoCarga ? ~Q0 : 1'bz;  // Controlled_Inverter controlled_inverter_4
  assign controlled_buffer_4_out = ModoCarga ? Q0 : 1'bz;  // Controlled_Buffer controlled_buffer_4

  // Notes on the sheet:
  //   Se não estiver, não vai mudar informação dos FlipFlops
  //   Só libera informação de buffer estiver ativo
endmodule
