// Logisim project Questao 2 lista 3.circ as structural Verilog: 1 circuit, main circuit main
module main (
  input  in_1,
  input  in_2,
  input  in_3,
  input  in_4
);

  wire and_1_out, and_2_out, or_1_out;

  and and_1 (and_1_out, in_1, in_3);
  and and_2 (and_2_out, in_1, in_2);
  or or_1 (or_1_out, and_1_out, and_2_out);
  _7_Segment_Display u_7_segment_display_1 (
    .g(or_1_out), .f(or_1_out), .a(or_1_out), .e(or_1_out), .d(or_1_out));  // open: b, c, dp
endmodule
