// Logisim project Questão 3.circ as structural Verilog: 1 circuit, main circuit main
module main (
  input  A,
  input  B,
  input  C,
  input  D,
  output out_5
);

  wire xnor_1_out, xnor_2_out;

  xnor xnor_1 (xnor_1_out, A, C);
  xnor xnor_2 (xnor_2_out, B, D);
  and and_1 (out_5, xnor_1_out, xnor_2_out);
endmodule
