// Logisim project Questao 5 lista 3.circ as structural Verilog: 1 circuit, main circuit main
module main (
  input  in_1,
  input  in_2,
  input  in_3,
  input  in_4,
  input  in_5,
  input  in_6,
  input  in_7,
  input  in_8,
  input  in_9,
  input  in_10,
  output out_11,
  output out_12,
  output out_13,
  output out_14
);

  or or_1 (out_13, in_8, in_3, in_4, in_7);
  or or_2 (out_12, in_5, in_6, in_7, in_8);
  or or_3 (out_11, in_9, in_10);
  or or_4 (out_14, in_2, in_4, in_8, in_6, in_10);

  // Other names for the same wires on the sheet: A = out_11; B = out_12; C = in_8; D = in_7; E = in_6; F = in_10
endmodule
