// Logisim project Questão 7 b).circ as structural Verilog: 1 circuit, main circuit main
module main (
  input  A,
  input  B,
  input  C,
  input  D,
  input  E,
  input  F,
  input  G,
  output out_8
);

  not not_1 (out_8, G);

  // Notes on the sheet:
  //   Para um número de 7 bits=> ABCDEFG
endmodule
