// Logisim project Projeto_PCL_Fase3.circ as structural Verilog: 11 circuits, main circuit ula
module ula (
  input  [7:0] Operando_1,
  input  [7:0] Operando_2,
  input  [3:0] Seletor,
  output [7:0] \Saída 
);

  wire comparator_1_eq, comparator_2_eq, comparator_3_lt, comparator_4_eq, comparator_4_lt, or_2_out;
  wire [7:0] adder_1_out, and_1_out, bit_extender_1_out, bit_extender_2_out, bit_extender_3_out,
       bit_extender_4_out, divider_1_out, multiplier_1_out, or_1_out, subtractor_1_out;

  assign and_1_out = Operando_1 & Operando_2;  // AND_Gate and_1, 8 bits wide
  assign or_1_out = Operando_1 | Operando_2;  // OR_Gate or_1, 8 bits wide
  Comparator comparator_1 (.a(Operando_1), .b({8{1'b0}}), .eq(comparator_1_eq));  // open: gt, lt
  Adder adder_1 (.a(Operando_1), .b(Operando_2), .out(adder_1_out));  // open: cin, cout
  Subtractor subtractor_1 (.a(Operando_1), .b(Operando_2), .out(subtractor_1_out));  // open: bin, bout
  Multiplier multiplier_1 (.a(Operando_1), .b(Operando_2), .out(multiplier_1_out));  // open: cin, cout
  Divider divider_1 (.a(Operando_1), .b(Operando_2), .out(divider_1_out));  // open: upper, rem
  Comparator comparator_2 (.a(Operando_1), .b(Operando_2), .eq(comparator_2_eq));  // open: gt, lt
  Comparator comparator_3 (.a(Operando_1), .b(Operando_2), .lt(comparator_3_lt));  // open: gt, eq
  Comparator comparator_4 (.a(Operando_1), .b(Operando_2), .eq(comparator_4_eq), .lt(comparator_4_lt));  // open: gt
  assign bit_extender_1_out = {{7{1'b0}}, comparator_1_eq};  // Bit_Extender bit_extender_1
  assign bit_extender_2_out = {{7{1'b0}}, comparator_2_eq};  // Bit_Extender bit_extender_2
  assign bit_extender_3_out = {{7{1'b0}}, comparator_3_lt};  // Bit_Extender bit_extender_3
  or or_2 (or_2_out, comparator_4_eq, comparator_4_lt);
  assign bit_extender_4_out = {{7{1'b0}}, or_2_out};  // Bit_Extender bit_extender_4
  Multiplexer #(.select(4), .width(8), .enable("false")) multiplexer_1 (
    .in0(and_1_out), .in1(or_1_out), .in2(bit_extender_1_out), .in3(adder_1_out), .in4(subtractor_1_out),
    .in5(multiplier_1_out), .in6(divider_1_out), .in7(bit_extender_2_out), .in8(bit_extender_3_out),
    .in9(bit_extender_4_out), .out(\Saída ), .sel(Seletor));  // open: in10, in11, in12, in13, in14, in15

  // Notes on the sheet:
  //   E 0000
  //   Ou 0001
  //   Não Logico 0010
  //   Add 0011
  //   sub 0100
  //   Mult. 0101
  //   Div.  0110
  //   Igual 0111
  //   Menor 1000
  //   Menor igual 1001
  //   João Lucas Lima de Melo PCL 2019.1
endmodule

module Registrador (
  input  [7:0] Entrada_de_Dados,
  input  Clock,
  input  write,
  input  [3:0] Seletor_A,
  input  [3:0] Seletor_w,
  input  [3:0] Seletor_B,
  output Valor_R0,
  output [7:0] \Saída_A ,
  output [7:0] \Saída_B 
);

  wire comparator_1_eq, demultiplexer_1_out0, demultiplexer_1_out1, demultiplexer_1_out2,
       demultiplexer_1_out3, demultiplexer_1_out4, demultiplexer_1_out5, demultiplexer_1_out6,
       demultiplexer_1_out7, demultiplexer_1_out8, demultiplexer_1_out9, demultiplexer_1_out10,
       demultiplexer_1_out11, demultiplexer_1_out12, demultiplexer_1_out13, demultiplexer_1_out14,
       demultiplexer_1_out15, not_1_out;
  wire [7:0] R0_q, register_1_q, register_2_q, register_3_q, register_4_q, register_5_q, register_6_q,
       register_7_q, register_8_q, register_9_q, register_10_q, register_11_q, register_12_q, register_13_q,
       register_14_q, register_15_q;

  Demultiplexer #(.select(4), .enable("false")) demultiplexer_1 (
    .out0(demultiplexer_1_out0), .out1(demultiplexer_1_out1), .out2(demultiplexer_1_out2),
    .out3(demultiplexer_1_out3), .out4(demultiplexer_1_out4), .out5(demultiplexer_1_out5),
    .out6(demultiplexer_1_out6), .out7(demultiplexer_1_out7), .out8(demultiplexer_1_out8),
    .out9(demultiplexer_1_out9), .out10(demultiplexer_1_out10), .out11(demultiplexer_1_out11),
    .out12(demultiplexer_1_out12), .out13(demultiplexer_1_out13), .out14(demultiplexer_1_out14),
    .out15(demultiplexer_1_out15), .in(not_1_out), .sel(Seletor_w));
  not not_1 (not_1_out, write);
  Register R0 (.D(Entrada_de_Dados), .en(demultiplexer_1_out0), .Q(R0_q), .clk(Clock));  // open: clr
  Register register_1 (.D(Entrada_de_Dados), .en(demultiplexer_1_out1), .Q(register_1_q), .clk(Clock));  // open: clr
  Register register_2 (.D(Entrada_de_Dados), .en(demultiplexer_1_out2), .Q(register_2_q), .clk(Clock));  // open: clr
  Register register_3 (.D(Entrada_de_Dados), .en(demultiplexer_1_out3), .Q(register_3_q), .clk(Clock));  // open: clr
  Register register_4 (.D(Entrada_de_Dados), .en(demultiplexer_1_out4), .Q(register_4_q), .clk(Clock));  // open: clr
  Register register_5 (.D(Entrada_de_Dados), .en(demultiplexer_1_out5), .Q(register_5_q), .clk(Clock));  // open: clr
  Register register_6 (.D(Entrada_de_Dados), .en(demultiplexer_1_out6), .Q(register_6_q), .clk(Clock));  // open: clr
  Register register_7 (.D(Entrada_de_Dados), .en(demultiplexer_1_out7), .Q(register_7_q), .clk(Clock));  // open: clr
  Register register_8 (.D(Entrada_de_Dados), .en(demultiplexer_1_out8), .Q(register_8_q), .clk(Clock));  // open: clr
  Register register_9 (.D(Entrada_de_Dados), .en(demultiplexer_1_out9), .Q(register_9_q), .clk(Clock));  // open: clr
  Register register_10 (.D(Entrada_de_Dados), .en(demultiplexer_1_out10), .Q(register_10_q), .clk(Clock));  // open: clr
  Register register_11 (.D(Entrada_de_Dados), .en(demultiplexer_1_out11), .Q(register_11_q), .clk(Clock));  // open: clr
  Register register_12 (.D(Entrada_de_Dados), .en(demultiplexer_1_out12), .Q(register_12_q), .clk(Clock));  // open: clr
  Register register_13 (.D(Entrada_de_Dados), .en(demultiplexer_1_out13), .Q(register_13_q), .clk(Clock));  // open: clr
  Register register_14 (.D(Entrada_de_Dados), .en(demultiplexer_1_out14), .Q(register_14_q), .clk(Clock));  // open: clr
  Register register_15 (.D(Entrada_de_Dados), .en(demultiplexer_1_out15), .Q(register_15_q), .clk(Clock));  // open: clr
  Comparator comparator_1 (.a(R0_q), .b({8{1'b0}}), .eq(comparator_1_eq));  // open: gt, lt
  not not_2 (Valor_R0, comparator_1_eq);
  Multiplexer #(.select(4), .width(8), .enable("false")) multiplexer_1 (
    .in0(R0_q), .in1(register_1_q), .in2(register_2_q), .in3(register_3_q), .in4(register_4_q),
    .in5(register_5_q), .in6(register_6_q), .in7(register_7_q), .in8(register_8_q), .in9(register_9_q),
    .in10(register_10_q), .in11(register_11_q), .in12(register_12_q), .in13(register_13_q),
    .in14(register_14_q), .in15(register_15_q), .out(\Saída_A ), .sel(Seletor_A));
  Multiplexer #(.select(4), .width(8), .enable("false")) multiplexer_2 (
    .in0(R0_q), .in1(register_1_q), .in2(register_2_q), .in3(register_3_q), .in4(register_4_q),
    .in5(register_5_q), .in6(register_6_q), .in7(register_7_q), .in8(register_8_q), .in9(register_9_q),
    .in10(register_10_q), .in11(register_11_q), .in12(register_12_q), .in13(register_13_q),
    .in14(register_14_q), .in15(register_15_q), .out(\Saída_B ), .sel(Seletor_B));
endmodule

module \Integração_ULA_Registrador  (
  input  Read_Write_ctrl,
  input  [2:0] Seletor_de_Entrada_de_Dados,
  input  [3:0] Seletor_w,
  input  [3:0] \Seletor_de_operação_ULA ,
  input  [3:0] Seletor_Registrador_Operando_A,
  input  [3:0] Seletor_Registrador_Operando_B,
  output Valor_R0
);

  wire registrador_1_p7, registrador_1_p8;
  wire [7:0] multiplexer_1_out, ula_1_p4;

  Multiplexer #(.select(3), .width(8)) multiplexer_1 (
    .in0(ula_1_p4), .out(multiplexer_1_out), .sel(Seletor_de_Entrada_de_Dados));  // open: in1, in2, in3, in4, in5, in6, in7, en
  // Registrador registrador_1: pin names not known; wires that end beside it: Read_Write_ctrl, Seletor_w, multiplexer_1_out, Seletor_Registrador_Operando_A, Seletor_Registrador_Operando_B, Valor_R0, registrador_1_p7, registrador_1_p8
  // ula ula_1: pin names not known; wires that end beside it: registrador_1_p8, registrador_1_p7, \Seletor_de_operação_ULA , ula_1_p4
endmodule

module pc_ctl (
  input  [3:0] Op,
  input  R0,
  output [1:0] out_3
);

  wire and_2_out, and_3_out, not_1_out, not_2_out, not_3_out, not_4_out, not_5_out;

  not not_1 (not_1_out, Op[0]);
  and and_1 (out_3[1], Op[3], Op[2], Op[1], not_1_out, R0);
  and and_2 (and_2_out, Op[2], Op[2], Op[1], not_1_out, not_2_out);
  not not_2 (not_2_out, R0);
  not not_3 (not_3_out, Op[1]);
  and and_3 (and_3_out, not_3_out, Op[2], Op[3]);
  not not_4 (not_4_out, Op[2]);
  not not_5 (not_5_out, Op[3]);
  or or_1 (out_3[0], and_2_out, and_3_out, not_4_out, not_5_out);
endmodule

module MI (
  input  [7:0] Operando,
  input  load,
  input  count,
  input  Clock,
  output [11:0] Entrada_IR,
  output [7:0] Saida_PC
);

  Counter #(.trigger("falling")) counter_1 (
    .load(load), .D(Operando), .count(count), .Q(Saida_PC), .clk(Clock));  // open: carry, clr
  ROM #(.dataWidth(12)) rom_1 (.addr(Saida_PC), .data(Entrada_IR));  // open: sel

  // Notes on the sheet:
  //   contents of rom_1 (hex, n*v repeats v):
  //   b00 c00 d10 b0a d20 b01 d30 812 200 e0e 331 d10 b01 e07 d01 c00 f00
endmodule

module IR (
  input  [11:0] \Saída_MI ,
  input  Clock,
  output [11:0] out_3
);

  Register #(.width(12)) register_1 (.D(\Saída_MI ), .Q(out_3), .clk(Clock));  // open: en, clr
endmodule

module MD (
  input  [7:0] \Endereço ,
  input  [7:0] Valor_a_ser_armazenado,
  input  Clock,
  input  STR,
  input  LDA,
  output [7:0] Valor_a_ser_retornado
);

  wire or_1_out;

  or or_1 (or_1_out, LDA, STR);
  RAM #(.bus("separate")) ram_1 (
    .addr(\Endereço ), .din(Valor_a_ser_armazenado), .data(Valor_a_ser_retornado), .str(STR), .sel(or_1_out),
    .clk(Clock), .ld(LDA));  // open: clr
endmodule

module IDEC (
  input  [11:0] Entrada_Operando_EndRegs,
  output [3:0] EndRegsY,
  output [3:0] EndRegsX,
  output [3:0] \Operação ,
  output [7:0] \Endereço 
);

  BitSelector #(.width(12), .group(4)) bitselector_1 (.in(Entrada_Operando_EndRegs), .out(EndRegsY), .sel(2'b00));
  BitSelector #(.width(12), .group(4)) bitselector_2 (.in(Entrada_Operando_EndRegs), .out(EndRegsX), .sel(2'b01));
  BitSelector #(.width(12), .group(4)) bitselector_3 (.in(Entrada_Operando_EndRegs), .out(\Operação ), .sel(2'b10));
  BitSelector #(.width(12), .group(8)) bitselector_4 (.in(Entrada_Operando_EndRegs), .out(\Endereço ), .sel(1'b0));
endmodule

module CTLU (
  input  [3:0] Operando,
  input  R0,
  output [2:0] rin_ctl,
  output rw_ctl,
  output [1:0] rd_ctl,
  output [1:0] pc_ctl,
  output rm_ctl,
  output wm_ctl
);

  wire and_2_out, and_3_out, not_1_out, not_2_out, not_3_out, not_4_out, not_5_out;

  Comparator #(.width(4)) comparator_1 (.a(Operando), .b(4'b1100), .eq(rw_ctl));  // open: gt, lt
  Multiplexer #(.select(4), .width(3)) multiplexer_1 (
    .in0(3'b000), .in1(3'b000), .in2(3'b000), .in3(3'b000), .in4(3'b000), .in5(3'b000), .in6(3'b000),
    .in7(3'b000), .in8(3'b000), .in9(3'b000), .in10(3'b001), .in11(3'b010), .in12(3'b000), .in13(3'b011),
    .in14(3'b100), .in15(3'b111), .out(rin_ctl), .sel(Operando));  // open: en
  Multiplexer #(.select(4), .width(2)) multiplexer_2 (
    .in0(2'b00), .in1(2'b00), .in2(2'b00), .in3(2'b00), .in4(2'b00), .in5(2'b00), .in6(2'b00), .in7(2'b00),
    .in8(2'b00), .in9(2'b00), .in10(2'b00), .in11(2'b00), .in12(2'b10), .in13(2'b10), .in14(2'b01),
    .in15(2'b01), .out(rd_ctl), .sel(Operando));  // open: en
  Multiplexer #(.select(4)) multiplexer_3 (
    .in0(1'b0), .in1(1'b0), .in2(1'b0), .in3(1'b0), .in4(1'b0), .in5(1'b0), .in6(1'b0), .in7(1'b0),
    .in8(1'b0), .in9(1'b0), .in10(1'b1), .in11(1'b0), .in12(1'b1), .in13(1'b0), .in14(1'b0), .in15(1'b0),
    .out(rm_ctl), .sel(Operando));  // open: en
  not not_1 (not_1_out, Operando[0]);
  and and_1 (pc_ctl[1], Operando[3], Operando[2], Operando[1], not_1_out, R0);
  and and_2 (and_2_out, Operando[2], Operando[2], Operando[1], not_1_out, not_2_out);
  not not_2 (not_2_out, R0);
  not not_3 (not_3_out, Operando[1]);
  and and_3 (and_3_out, not_3_out, Operando[2], Operando[3]);
  not not_4 (not_4_out, Operando[2]);
  or or_1 (pc_ctl[0], and_2_out, and_3_out, not_4_out, not_5_out);
  not not_5 (not_5_out, Operando[3]);

  assign wm_ctl = rm_ctl;
endmodule

module ARQ38 (
  input  [7:0] in_1,
  input  in_2,
  output [7:0] out_3
);

  wire Clock, comparator_1_eq, demultiplexer_1_out1, demultiplexer_1_out2, R0, rm_ctl, RwCTL,
       \seleção_1_lda , \seleção_1_str , wm_ctl;
  wire [1:0] pc_ctl, RdCTL;
  wire [2:0] RinCTL;
  wire [3:0] EndRegX, EndRegY, \idec_1_operação , multiplexer_2_out, multiplexer_3_out, Op;
  wire [7:0] End, multiplexer_1_out, Op1, Op2, \SaídaPC , \ula_1_saída ;
  wire [11:0] \Instrução , \SaídaMI ;

  Clock clock_1 (.out(Clock));
  \Seleção  \seleção_1  (.Operando(Op), .LDA(\seleção_1_lda ), .STR(\seleção_1_str ), .Sinal(rm_ctl));
  MD md_1 (
    .\Endereço (End), .Valor_a_ser_armazenado(Op1), .Valor_a_ser_retornado(out_3), .LDA(\seleção_1_lda ),
    .STR(\seleção_1_str ), .Clock(Clock));
  CTLU ctlu_1 (
    .Operando(\idec_1_operação ), .rin_ctl(RinCTL), .rw_ctl(RwCTL), .rd_ctl(RdCTL), .pc_ctl(pc_ctl),
    .rm_ctl(rm_ctl), .R0(R0), .wm_ctl(wm_ctl));
  ula ula_1 (.Operando_1(Op1), .Operando_2(Op2), .Seletor(Op), .\Saída (\ula_1_saída ));
  IDEC idec_1 (
    .Entrada_Operando_EndRegs(\Instrução ), .\Operação (\idec_1_operação ));  // open: EndRegsY, EndRegsX, Endereço
  Comparator #(.width(4)) comparator_1 (.a(Op), .b(4'b1100), .eq(comparator_1_eq));  // open: gt, lt
  Multiplexer #(.select(3), .width(8)) multiplexer_1 (
    .in0(\ula_1_saída ), .in1(out_3), .in2(End), .in3(Op2), .in4(\SaídaPC ), .out(multiplexer_1_out),
    .sel(RinCTL));  // open: in5, in6, in7, en
  Multiplexer #(.width(4)) multiplexer_2 (
    .in0(EndRegX), .in1(4'b0000), .out(multiplexer_2_out), .sel(comparator_1_eq));  // open: en
  Multiplexer #(.select(2), .width(4)) multiplexer_3 (
    .in0(4'b0000), .in1(4'b1111), .in2(EndRegX), .out(multiplexer_3_out), .sel(RdCTL));  // open: in3, en
  Registrador registrador_1 (
    .write(RwCTL), .Valor_R0(R0), .\Saída_A (Op1), .\Saída_B (Op2), .Seletor_w(multiplexer_3_out),
    .Entrada_de_Dados(multiplexer_1_out), .Seletor_A(multiplexer_2_out), .Seletor_B(EndRegY), .Clock(Clock));
  Demultiplexer #(.select(2)) demultiplexer_1 (
    .out1(demultiplexer_1_out1), .out2(demultiplexer_1_out2), .in(1'b1), .sel(pc_ctl));  // open: out0, out3, en
  IR ir_1 (.\Saída_MI (\SaídaMI ), .out_3(\Instrução ), .Clock(Clock));
  IDEC idec_2 (
    .Entrada_Operando_EndRegs(\Instrução ), .EndRegsY(EndRegY), .EndRegsX(EndRegX), .\Operação (Op),
    .\Endereço (End));
  MI mi_1 (
    .Operando(End), .load(demultiplexer_1_out2), .count(demultiplexer_1_out1), .Entrada_IR(\SaídaMI ),
    .Saida_PC(\SaídaPC ), .Clock(Clock));

  // Other names for the same wires on the sheet: ValorRetornado[7:0] = out_3
endmodule

module \Seleção  (
  input  [3:0] Operando,
  input  Sinal,
  output LDA,
  output STR
);

  wire not_1_out, not_2_out, not_3_out, not_4_out;

  not not_1 (not_1_out, Operando[2]);
  not not_2 (not_2_out, Operando[0]);
  not not_3 (not_3_out, Operando[1]);
  not not_4 (not_4_out, Operando[0]);
  and and_1 (LDA, Operando[3], not_1_out, Operando[1], not_2_out, Sinal);
  and and_2 (STR, Operando[3], Operando[2], not_3_out, not_4_out, Sinal);
endmodule
